// Digital circuit lab04-full_adder.dig as structural Verilog
module lab04_full_adder (
  input  A,
  input  B,
  input  Cin,
  output Sum,
  output Cout
);

  wire _4, _7400_1_pin3, _7400_1_pin6, _7400_1_pin10, _7400_2_pin3, _7400_2_pin8, _7400_2_pin11;

  _7400 _7400_1 (
    .pin1(A), .pin2(B), .pin3(_7400_1_pin3), .pin4(_7400_1_pin3), .pin5(A), .pin6(_7400_1_pin6), .pin7(1'b0),
    .pin8(_4), .pin9(_7400_1_pin6), .pin10(_7400_1_pin10), .pin11(_7400_1_pin10), .pin12(B),
    .pin13(_7400_1_pin3), .pin14(1'b1));
  _7400 _7400_2 (
    .pin1(_4), .pin2(Cin), .pin3(_7400_2_pin3), .pin4(_7400_2_pin3), .pin5(_7400_1_pin3), .pin6(Cout),
    .pin7(1'b0), .pin8(_7400_2_pin8), .pin9(Cin), .pin10(_7400_2_pin3), .pin11(_7400_2_pin11), .pin12(_4),
    .pin13(_7400_2_pin3), .pin14(1'b1));
  _7400 _7400_3 (
    .pin1(1'b0), .pin2(1'b0), .pin4(1'b0), .pin5(1'b0), .pin7(1'b0), .pin9(1'b0), .pin10(1'b0), .pin11(Sum),
    .pin12(_7400_2_pin11), .pin13(_7400_2_pin8), .pin14(1'b1));  // open: pin3, pin6, pin8
endmodule
